// Logisim project uart_rx.circ as structural Verilog: 2 circuits, main circuit main
module main (
  input  DIN,
  input  RST,
  output [7:0] DOUT,
  output DOUT_VLD
);

  wire and_1_out, and_2_out, clock_1_out, clock_2_out, clock_3_out, clock_4_out, clock_5_out, clock_6_out,
       clock_7_out, counter_1_carry, counter_2_carry, d_ff_1_q, d_ff_2_q, d_ff_3_q, d_ff_4_q,
       demultiplexer_1_out0, demultiplexer_1_out1, demultiplexer_1_out2, demultiplexer_1_out3,
       demultiplexer_1_out4, demultiplexer_1_out5, demultiplexer_1_out6, demultiplexer_1_out7, fsm_1_cc3,
       fsm_1_cc4, fsm_1_clr, fsm_1_read, multiplexer_1_out, not_1_out, not_2_out, or_1_out;
  wire [2:0] counter_2_q;

  Clock clock_1 (.out(clock_1_out));
  Clock clock_2 (.out(clock_2_out));
  D_Flip_Flop d_ff_1 (.D(DIN), .clk(clock_1_out), .Q(d_ff_1_q), .preset(RST));  // open: Qn, reset
  D_Flip_Flop d_ff_2 (.D(counter_1_carry), .clk(clock_3_out), .Q(d_ff_2_q), .reset(RST));  // open: Qn, preset
  Clock clock_3 (.out(clock_3_out));
  D_Flip_Flop d_ff_3 (.D(d_ff_1_q), .clk(clock_1_out), .Q(d_ff_3_q), .preset(RST));  // open: Qn, reset
  D_Flip_Flop d_ff_4 (.D(d_ff_3_q), .clk(clock_1_out), .Q(d_ff_4_q), .preset(RST));  // open: Qn, reset
  FSM fsm_1 (
    .DAT(d_ff_4_q), .CNT3(counter_2_carry), .CNT4(counter_1_carry), .CLK(clock_2_out), .RST(RST),
    .READ(fsm_1_read), .CC3(fsm_1_cc3), .CC4(fsm_1_cc4), .VLD(DOUT_VLD), .CLR(fsm_1_clr));
  Clock clock_4 (.out(clock_4_out));
  Clock clock_5 (.out(clock_5_out));
  Multiplexer multiplexer_1 (.in0(clock_5_out), .in1(d_ff_2_q), .out(multiplexer_1_out), .sel(fsm_1_read));
  Counter #(.max('hf), .width(4)) counter_1 (
    .clr(RST), .load(not_1_out), .up(1'b1), .count(fsm_1_cc4), .clk(clock_4_out), .D(4'b0000),
    .carry(counter_1_carry));  // open: Q
  not not_1 (not_1_out, fsm_1_cc4);
  Counter #(.max('h7), .width(3)) counter_2 (
    .clr(RST), .load(not_2_out), .up(1'b1), .count(fsm_1_cc3), .clk(multiplexer_1_out), .D(3'b000),
    .carry(counter_2_carry), .Q(counter_2_q));
  not not_2 (not_2_out, fsm_1_cc3);
  Demultiplexer #(.enable("true"), .select(3)) demultiplexer_1 (
    .out0(demultiplexer_1_out0), .out1(demultiplexer_1_out1), .out2(demultiplexer_1_out2),
    .out3(demultiplexer_1_out3), .out4(demultiplexer_1_out4), .out5(demultiplexer_1_out5),
    .out6(demultiplexer_1_out6), .out7(demultiplexer_1_out7), .in(d_ff_4_q), .sel(counter_2_q), .en(and_1_out));
  and and_1 (and_1_out, fsm_1_read, counter_1_carry);
  Clock clock_6 (.out(clock_6_out));
  or or_1 (or_1_out, RST, and_2_out);
  and and_2 (and_2_out, fsm_1_clr, clock_6_out);
  Clock clock_7 (.out(clock_7_out));
  T_Flip_Flop t_ff_1 (.T(demultiplexer_1_out0), .clk(clock_7_out), .Q(DOUT[0]), .reset(or_1_out));  // open: Qn, preset
  T_Flip_Flop t_ff_2 (.T(demultiplexer_1_out2), .clk(clock_7_out), .Q(DOUT[2]), .reset(or_1_out));  // open: Qn, preset
  T_Flip_Flop t_ff_3 (.T(demultiplexer_1_out4), .clk(clock_7_out), .Q(DOUT[4]), .reset(or_1_out));  // open: Qn, preset
  T_Flip_Flop t_ff_4 (.T(demultiplexer_1_out6), .clk(clock_7_out), .Q(DOUT[6]), .reset(or_1_out));  // open: Qn, preset
  T_Flip_Flop t_ff_5 (.T(demultiplexer_1_out1), .clk(clock_7_out), .Q(DOUT[1]), .reset(or_1_out));  // open: Qn, preset
  T_Flip_Flop t_ff_6 (.T(demultiplexer_1_out3), .clk(clock_7_out), .Q(DOUT[3]), .reset(or_1_out));  // open: Qn, preset
  T_Flip_Flop t_ff_7 (.T(demultiplexer_1_out5), .clk(clock_7_out), .Q(DOUT[5]), .reset(or_1_out));  // open: Qn, preset
  T_Flip_Flop t_ff_8 (.T(demultiplexer_1_out7), .clk(clock_7_out), .Q(DOUT[7]), .reset(or_1_out));  // open: Qn, preset

  // Notes on the sheet:
  //   Synchronize the input
  //   READ=1 chains CTR4 and CTR3 into CTR7
  //   Delay by one cycle
  //   G5 in CTR is Enable
  //   Allow only stable CLR
endmodule

module FSM (
  input  DAT,
  input  CNT3,
  input  CNT4,
  input  CLK,
  input  RST,
  output READ,
  output CC3,
  output CC4,
  output VLD,
  output CLR
);

  wire and_1_out, and_2_out, and_3_out, and_4_out, and_5_out, not_1_out, or_1_out, shift_register_1_p2,
       shift_register_1_p12, shift_register_1_p13, shift_register_1_p15, shift_register_1_p16;

  not not_1 (not_1_out, DAT);
  and and_1 (and_1_out, shift_register_1_p12, not_1_out);
  and and_2 (and_2_out, CNT3, shift_register_1_p13);
  and and_3 (and_3_out, CNT3, CNT4, READ);
  and and_4 (and_4_out, CNT4, shift_register_1_p15);
  and and_5 (and_5_out, CNT3, shift_register_1_p16);
  or or_1 (or_1_out, and_1_out, and_2_out, and_3_out, and_4_out, and_5_out, VLD);
  // Shift_Register #(.length(6)) shift_register_1: pin names not known; wires that end beside it: RST, shift_register_1_p2, or_1_out, CLK, VLD, 1'b1, 1'b0, 1'b0, 1'b0, 1'b0, 1'b0, shift_register_1_p12, shift_register_1_p13, READ, shift_register_1_p15, shift_register_1_p16, VLD
  nor nor_1 (shift_register_1_p2, shift_register_1_p12, shift_register_1_p13, READ, shift_register_1_p15, shift_register_1_p16, VLD);
  or or_2 (CC3, shift_register_1_p13, READ, shift_register_1_p16);
  or or_3 (CC4, READ, shift_register_1_p15);
  nor nor_2 (CLR, READ, shift_register_1_p15, shift_register_1_p16, VLD);
endmodule
